// Digital circuit mk36000.dig as structural Verilog
module mk36000 (
  input  nCE,
  input  A0,
  input  A1,
  input  A2,
  input  A3,
  input  A4,
  input  A5,
  input  A6,
  input  A7,
  input  A8,
  input  A9,
  input  A10,
  input  A11,
  input  A12,
  input  VCC,
  input  GND,
  output D0,
  output D1,
  output D2,
  output D3,
  output D4,
  output D5,
  output D6,
  output D7
);

  ROM #(.AddrBits(13), .Bits(8)) MK36000 (
    .A({A12, A11, A10, A9, A8, A7, A6, A5, A4, A3, A2, A1, A0}), .sel(nCE),
    .D({D7, D6, D5, D4, D3, D2, D1, D0}));
  PowerSupply powersupply_1 (.VDD(VCC), .GND(GND));

  // Notes on the sheet:
  //   nCE: pin 20
  //   A0: pin 8
  //   A1: pin 7
  //   A2: pin 6
  //   A3: pin 5
  //   A4: pin 4
  //   A5: pin 3
  //   A6: pin 2
  //   A7: pin 1
  //   A8: pin 23
  //   A9: pin 22
  //   A10: pin 19
  //   A11: pin 18
  //   A12: pin 21
  //   D0: pin 9
  //   D1: pin 10
  //   D2: pin 12
  //   D3: pin 13
  //   D4: pin 14
  //   D5: pin 15
  //   D6: pin 16
  //   D7: pin 17
  //   VCC: pin 24, default 1
  //   GND: pin 12
  //   MK36000 loads 5788005.u33
endmodule
